// Logisim project parfait.circ as structural Verilog: 2 circuits, main circuit main
module main (
);

  wire and_1_out, and_2_out, and_3_out, clock_1_out, not_1_out, or_1_out, or_2_out;
  wire [3:0] counter_1_q;

  Counter #(.width(4), .max('hf)) counter_1 (.Q(counter_1_q), .clk(clock_1_out));  // open: load, D, count, carry, clr
  Clock clock_1 (.out(clock_1_out));
  or or_1 (or_1_out, counter_1_q[2], counter_1_q[1]);
  or or_2 (or_2_out, counter_1_q[1], counter_1_q[0]);
  and and_1 (and_1_out, counter_1_q[3], or_1_out);
  and and_2 (and_2_out, and_1_out, or_2_out);
  not not_1 (not_1_out, and_1_out);
  LED led_1 (.in(and_3_out));
  and and_3 (and_3_out, counter_1_q[3], not_1_out);
  LED led_2 (.in(not_1_out));
  LED led_3 (.in(and_1_out));
  LED led_4 (.in(and_2_out));

  // Notes on the sheet:
  //   X
  //   C
  //   V
  //   R
endmodule

module test (
);

  wire and_1_out, and_2_out, and_3_out, and_4_out, and_5_out, and_6_out, button_1_out, clock_1_out,
       not_1_out, not_2_out, not_3_out, not_4_out, not_5_out, or_1_out, or_2_out, or_3_out;
  wire [3:0] counter_1_q;

  Counter #(.width(4), .max('hf)) counter_1 (
    .Q(counter_1_q), .clk(clock_1_out), .clr(button_1_out));  // open: load, D, count, carry
  Clock clock_1 (.out(clock_1_out));
  Button button_1 (.out(button_1_out));
  not not_1 (not_1_out, counter_1_q[2]);
  not not_2 (not_2_out, counter_1_q[1]);
  and and_1 (and_1_out, counter_1_q[3], counter_1_q[1]);
  and and_2 (and_2_out, counter_1_q[3], counter_1_q[2]);
  and and_3 (and_3_out, counter_1_q[3], counter_1_q[1]);
  and and_4 (and_4_out, counter_1_q[3], counter_1_q[2], counter_1_q[0]);
  not not_3 (not_3_out, counter_1_q[2]);
  not not_4 (not_4_out, counter_1_q[1]);
  not not_5 (not_5_out, counter_1_q[3]);
  and and_5 (and_5_out, not_1_out, not_2_out);
  or or_1 (or_1_out, and_1_out, and_2_out);
  or or_2 (or_2_out, and_3_out, and_4_out);
  and and_6 (and_6_out, counter_1_q[3], not_3_out, not_4_out);
  or or_3 (or_3_out, not_5_out, and_5_out);
  LED C (.in(or_3_out));
  LED V (.in(or_1_out));
  LED R (.in(or_2_out));
  LED X (.in(and_6_out));
endmodule
